# Fritzing sketch Automatic_Catbot (saved by Fritzing 0.9.3b)
breadboards: 1

parts:
  Componente1 = Arduino Uno (Rev3)
  J1 = Basic Servo
  J2 = Basic Servo
  hc-sr1 = hc-sr04
  VCC2 = 4 x AAA Battery Mount
  SERVO1 = Tower Pro SG90 servo [part_number=101246]
  IR1 = TSOP312.., 314.. [package=THT]
  R1 = Resistor [tolerance=±5% resistance=220 package="2512 [SMD]"]
  VCC3 = 4 x AAA Battery Mount  # not connected
  U1 = SWITCH-SPST-2 [package=switch-spst-vertical]  # not connected
  U2 = SWITCH-SPST-2 [package=switch-spst-vertical]  # not connected

nets:
  N1: Componente1.D8, J1.pulse
  N2: Componente1.D9_PWM, J2.pulse
  N3: Componente1.D10_PWM/SS, SERVO1.Signal
  N4: Componente1.D11_PWM/MOSI, hc-sr1.Echo
  N5: Componente1.D12/MISO, hc-sr1.Trig
  N6: Componente1.D7, R1.Pin_0
  5V: Componente1.5V, hc-sr1.VCC
  GND: Componente1.GND, J1.gnd, J2.gnd, hc-sr1.GND, SERVO1.GND, IR1.Vs
  VIN: Componente1.VIN, SERVO1.+5V, IR1.Data
  N7: J1.vcc, VCC2.+
  N8: IR1.GND, R1.Pin_1

notes:
  LEFT Servo
  SM-S4303R
  RIGHT Servo
  SM-S4303R
  Ultrasonic Servo
  IR Receiver

custom parts:
  Tower Pro SG90 servo: Original file by John De Cristofaro http://www.adafruit.com/products/1449 Adafruit Feedback Servo (Small) Edited by: e-radionica.com 28/9/2015

// code stored in the sketch: MKR1000_temp y humedad con aRest.ino


// Import required libraries
#include <SPI.h>
#include <WiFi101.h>
#include <PubSubClient.h>
#include <aREST.h>
#include <Servo.h>

// Servos
int azimut = 90;
int elevation = 90;
Servo azimut_servo;
Servo elevation_servo;
int pin_azimut = 4;
int pin_elevation = 5;

// Servo Control Pins
int left = 7;
int right = 8;
int up = 9;
int down = 10;


// Status
int status = WL_IDLE_STATUS;

// Clients
WiFiClient wifiClient;
PubSubClient client(wifiClient);

// Create aREST instance
aREST rest = aREST(client);

// Device ID for the device on the cloud (should be 6 characters long)
char * device_id = "221422";

// WiFi parameters
char ssid[] = "my SSID";
char password[] = "my PASSWORD";

// Variables to be exposed to the API
int temperature;
int humidity;

// Declare functions to be exposed to the API
int ledControl(String command);

// Callback function for the cloud connection
void callback(char* topic, byte* payload, unsigned int length);

void setup(void)
{
  //Servos
  azimut_servo.attach(pin_azimut);
  elevation_servo.attach(pin_elevation);
  azimut_servo.write(azimut);
  elevation_servo.write(elevation);

  // Start Serial
  Serial.begin(115200);

  // Set callback
  client.setCallback(callback);

  // Init variables and expose them to REST API
  temperature = 24;
  humidity = 40;
  rest.variable("temperature", &temperature);
  rest.variable("humidity", &humidity);

  // Function to be exposed
  rest.function("led", ledControl);

  // Give name and ID to device (ID should be 6 characters long)
  rest.set_id(device_id);
  rest.set_name("mkr1000");

  // Connect to WiFi
  while (status != WL_CONNECTED) {
    Serial.print("Attempting to connect to SSID: ");
    Serial.println(ssid);
    status = WiFi.begin(ssid, password);

    // Wait 10 seconds for connection:
    delay(10000);
  }
  Serial.println("WiFi connected");

}

void loop() {

  // Connect to the cloud
  rest.handle(client);

  // Servos
  
  if ((digitalRead(left) == HIGH) && (azimut > 50)) {
    azimut = azimut - 1;
    azimut_servo.write(azimut);
    delay (200);
  }
  if ((digitalRead(right) == HIGH) && (azimut < 130)) {
    azimut = azimut + 1;
    azimut_servo.write(azimut);
    delay (200);
  }
  if ((digitalRead(down) == HIGH) && (elevation > 40)) {
    elevation = elevation - 1;
    elevation_servo.write(elevation);
    delay (200);
  }
  if ((digitalRead(up) == HIGH) && (elevation < 110)) {
    elevation = elevation + 1;
    elevation_servo.write(elevation);
    delay (200);
  }
  Serial.print("Azimut = ");
  Serial.println(azimut);
  Serial.print("Elevation = ");
  Serial.println(elevation);
}

// Custom function accessible by the API
int ledControl(String command) {

  // Get state from command
  int state = command.toInt();

  digitalWrite(6, state);
  return 1;
}


// Handles message arrived on subscribed topic(s)
void callback(char* topic, byte* payload, unsigned int length) {

  // Handle
  rest.handle_callback(client, topic, payload, length);


}

// code stored in the sketch: robot.ino


// code stored in the sketch: Web_MKR1000_sensor_temp__DHT11_lumi_porce_bateria.ino
//Añadimos la libreria WIFI
#include <WiFi101.h>
#include <TimeLib.h>

//Añadimos la libreria con la cual trabaja nuestro sensor DHT11
#include "DHT.h"

/*VARIABLES LEDS*/
#define ledVerde 3
#define ledAzul 4
#define ledRojo 5

/*VARIABLES DHT11*/
#define DHTPIN 1
#define DHTTYPE DHT11
DHT dht(DHTPIN, DHTTYPE);  //Indica el pin con el que trabajamos y el tipo de sensor
float temperatura = 0;
float humedad = 0;

/*VARIABLES LUMINOSIDAD*/
int luminosidad;
String luz = "Penumbra";

/*VARIABLES FILTRO PASO BAJO*/
const int numLecturas = 30; // Número de lecturas para media
int lecturas[numLecturas]; // Array de muestras
int lecturaActual = 0; // La lectura por la que vamos
int total = 0; // Total de las 10 muestras
int media = 0; // Media obtenida

/*VARIABLES SERVIDOR WEB*/
char nombreWiFi[] = "JAZZTEL_MmTq";
char claveWiFi[] = "qup4h7mjg3ch";
int estado = WL_IDLE_STATUS;
IPAddress ip (192, 168, 1, 156);
WiFiServer server(80);

/*VARIABLES BATERÍA*/
#define ledBateria 2
boolean estaCargando = true;
int umbralBateria = 2000; // Si está por debajo de este umbral está funcionando con batería
int totalMinutos = 793; // Para una batería de 2000 mAh
int tiempoRestante = 793; // Siempre comenzamos con carga completa
int porcentajeRestante = 100;

/*******************************************************************/
/*SETUP*/
/*******************************************************************/
void setup() {
  // Monitor serie
  Serial.begin(9600);

  // Configurar LEDs
  configurarLEDs();

  // Configurar DHT11
  configurarDHT11();

  // Cambiar resolución para sensor luminosidad
  analogReadResolution(12);

  // Configurar servidor web
  configurarServidorWeb();

  // Inicializamos el reloj
  inicializarReloj();
}

/*******************************************************************/
/*LOOP*/
/*******************************************************************/
void loop() {
  //1. Lectura de temperatura, humedad y luminosidad
  lecturaSensor();

  //2. Petición del cliente web
  responderPeticionCliente();

  //3. Comprobar la batería
  comprobarCargaBateria();

  // Solo comprobamos cuanto tiempo queda si no está cargando
  // Cuando se esté almentando de la batería
  if (!estaCargando)
  {
    // Calcular el tiempo restante de batería
    calcularTiempoRestanteBateria();
  }
}


/*******************************************************************/
/* GESTIÓN DE BATERÍA */
/*******************************************************************/

// Comprueba si la batería está cargando
void comprobarCargaBateria()
{
  // Leemos el pin analógico
  int valorA2 = analogRead(ledBateria);


  // Comprobamos si está cargando la batería
  if (valorA2 < umbralBateria)
  {
    // Si no está cargando pero viene de la carga
    if (estaCargando)
    {
      // Inicializamos el reloj
      inicializarReloj();
    }

    estaCargando = false;
  }
  else
  {
    // Marcamos que ya no está cargando
    estaCargando = true;
  }
}

// Pone en hora el reloj
void inicializarReloj()
{
  // Comenzamos la cuenta en el 00:00
  setTime(0, 0, 0, 1, 1, 2016);
}

// Calcular tiempo restante batería
void calcularTiempoRestanteBateria()
{
  // Obtenemos las minutos que llevamos
  int minutos = minute() + (hour() * 60);

  // Tiempo restante de batería
  tiempoRestante = totalMinutos - minutos;

  // Porcentaje restante
  porcentajeRestante = (tiempoRestante * 100) / totalMinutos;
}
/*******************************************************************/
/* CONFIGURACIÓN LEDS*/
/*******************************************************************/

// Función que configura los LEDs
void configurarLEDs()
{
  // Modos de los pines
  pinMode(ledVerde, OUTPUT);
  pinMode(ledAzul, OUTPUT);
  pinMode(ledRojo, OUTPUT);
}

/*******************************************************************/
/*DHT11*/
/*******************************************************************/
// Función que configura DHT11
void configurarDHT11()
{
  // Iniciamos libreria DHT11
  dht.begin();

  // Iniciamos el array
  for (int i = 0; i < numLecturas; i++)
  {
    lecturas[i] = 0;
  }
}

// Función que lee el sensor de temperatura DHT11
void lecturaSensor()
{
  digitalWrite(ledAzul, HIGH);

  // Eliminando la última muestra
  total = total - lecturas[lecturaActual];

  // Lectura humedad, temperatura y humedad
  int h = dht.readHumidity();  //Guarda la lectura de la humedad en la variable float h
  int t = dht.readTemperature();  //Guarda la lectura de la temperatura en la variable float t
  luminosidad = analogRead(A1);


  lecturas[lecturaActual] = t;

  // Añadimos la lectura al total
  total = total + lecturas[lecturaActual];

  // Incrementamos el índice del array
  lecturaActual = lecturaActual + 1;

  // Comprabamos que no nos salimos del tamaño del array
  if (lecturaActual >= numLecturas)
  {
    lecturaActual = 0;
  }

  // Calculamos la media
  media = total / numLecturas;

  //Serial.print("valor sin filtro= ");
  // Serial.println(t);

  // Calculo
  //temperatura = (500*media / 4096) - 168;
  temperatura = t;
  humedad = h;
  //temperatura = (media*5/4096)*100;


  // Calculo luz, penumbra u oscuridad
  if (luminosidad > 750) {
    luz = "Oscuridad";
  }
  else if (luminosidad < 550) {
    luz = "Luminoso";
  }
  else {
    luz = "Penumbra";
  }

  Serial.print("Temperatura = ");
  Serial.print(temperatura);
  Serial.println("C");
  Serial.print("Humedad = ");
  Serial.print(h);
  Serial.println("%");
  Serial.print("Luminosidad = ");
  Serial.println(luminosidad);
  Serial.print("luz = ");
  Serial.println(luz);

  delay(500);

  digitalWrite(ledAzul, LOW);

  delay(500);
}

/*******************************************************************/
/*SERVIDOR WEB*/
/*******************************************************************/

// Función que configura el servidor web
void configurarServidorWeb()
{
  digitalWrite(ledRojo, HIGH);
  digitalWrite(ledVerde, HIGH);

  // Chequeamos que tenemos módulo WiFi
  if (WiFi.status() == WL_NO_SHIELD)
  {
    digitalWrite(ledVerde, LOW);
    Serial.println("No hay módulo WiFi");

    while (true);
  }

  // Configurar ip estática
  WiFi.config(ip);

  // Conexión con la red WiFi
  while (estado != WL_CONNECTED)
  {
    // Mostramos mensajes
    Serial.print("Intentando conectar a WiFi con nombre ");
    Serial.println(nombreWiFi);

    // Conexión con red WiFi
    estado = WiFi.begin(nombreWiFi, claveWiFi);

    delay(10000);
  }

  Serial.print("Conectado a red WiFi con la IP ");
  Serial.println(ip);

  // Empezar a escuchar conexiones entrantes
  server.begin();

  digitalWrite(ledRojo, LOW);
}

// Función que responde a la petición de un cliente web
void responderPeticionCliente()
{
  // Cliente que se conecta
  // Lo recogemos con la función available de la clase server.
  // Si no hay cliente devuelve falso (false)
  WiFiClient cliente = server.available();

  if (cliente)
  {
    // Variable para detectar final de la petición
    boolean lineaActualenBlanco = true;

    // Repetimos mientras el cliente esté conectado.
    // Estará conectado mientras tengamos datos que leer
    while (cliente.connected())
    {
      // Nos devuelve si hay información pendiente de ser leída
      // En caso de no haber, devuelve falso (false)
      if (cliente.available())
      {
        // Leemos byte a byte y lo almacenamos en un char (carácter a carácter)
        char peticion = cliente.read();
        Serial.print(peticion);

        // Comprobamos si es una nueva línea
        if (peticion == '\n' && lineaActualenBlanco)
        {
          int temperaturaInt = (int)temperatura;
          int humedadInt = (int)humedad;
          // Cabecera para informar que estamos enviando una página web
          // El código 200 es un código de estado informando que la petición es correcta
          // Un código común es el 404 que informa que el recurso no se ha encontrado
          cliente.println("HTTP/1.1 200 OK");
          cliente.println("Content-type:text/html");
          cliente.println();
          //********************************************************************************
          cliente.println("<!DOCTYPE html>");
          cliente.println("<html lang=\"en\">");
          cliente.println("<head>");
          cliente.println("<meta charset=\"UTF-8\">");
          cliente.println("<title>Sensor de temperatura MKR1000</title>");
          cliente.println("<meta charset=\"UTF-8\">");
          cliente.println("<title>Sensor de temperatura MKR1000</title>");
          cliente.println("<meta name=\"viewport\" content=\"width=device-width, user-scalable=no, initial-scale=1.0, maximum-scale=1.0, minimum-scale=1.0\">");
          cliente.println("<!-- Latest compiled and minified CSS -->");
          cliente.println("<link rel=\"stylesheet\" href=\"https://maxcdn.bootstrapcdn.com/bootstrap/3.3.6/css/bootstrap.min.css\" integrity=\"sha384-1q8mTJOASx8j1Au+a5WDVnPi2lkFfwwEAa8hDDdjZlpLegxhjVME1fgjWPGmkzs7\" crossorigin=\"anonymous\">");
          cliente.println("<style type=\"text/css\">");
          cliente.println("header{");
          cliente.println("background: #2980b9;");
          cliente.println("color: white;");
          cliente.println("}");
          cliente.println("aside{");
          cliente.println("background: #0f5786;");
          cliente.println("color: white;");
          cliente.println("}");
          cliente.println("footer{");
          cliente.println("background: #2980b9;");
          cliente.println("color: white;");
          cliente.println("}");
          cliente.println("#h1Temp{");
          cliente.println("font-size: 65px;");
          cliente.println("}");
          cliente.println("</style>");
          cliente.println("</head>");
          cliente.println("<body>");
          cliente.println("<div class=\"container\">");
          cliente.println("<header class=\"container\">");
          cliente.println("<h1>Control temperatura MKR1000</h1> ");
          cliente.println("<h3>Mi casa</h3>");
          cliente.println("</header>");
          cliente.println("<div class=\"container\">");
          cliente.println("<section class=\"row\">");
          cliente.println("<div class=\"col-xs-12 col-sm-8 col-md-8 col-lg-8\">");
          cliente.print("<h1 id=\"h1Temp\" class=\"text-center\">");
          cliente.print("Temp: ");
          cliente.print(temperaturaInt);
          cliente.println("º</h1>");
          cliente.print("<h1 id=\"h1Temp\" class=\"text-center\">");
          cliente.print("Hum: ");
          cliente.print(humedadInt);
          cliente.println("%</h1>");
          cliente.print("<h1 id=\"h1Temp\" class=\"text-center\">");
          cliente.print(luz);
          cliente.println("</h1>");
          cliente.println("</div>");
          cliente.println("<aside class=\"col-xs-12 col-sm-4 col-md-4 col-lg-4\">");
          cliente.println("<div class=\"text-center\">");
          cliente.print("<div>Bateria ");
          cliente.print(porcentajeRestante);
          cliente.println("%</div>");
          cliente.print("<progress class=\"progress\" value=\"");
          cliente.print(porcentajeRestante);
          cliente.println("\" max=\"100\"></progress>");
          cliente.println("</div>");
          cliente.println("<h3 class=\"text-center\">Arduino MKR1000</h3>");
          cliente.println("<p><img src=\"http://i0.wp.com/programarfacil.com/wp-content/uploads/2016/04/mkr1000-difuminada.jpg?w=450\" alt=\"Arduino MKR1000\" class=\"img-responsive center-block\"></p>");
          //cliente.println("<p><img src=\"https://rojoygualda.files.wordpress.com/2012/08/img_ch47usarmy.jpg\" alt=\"Arduino MKR1000\" class=\"img-responsive center-block\"></p>");
          cliente.println("</aside>");
          cliente.println("</section>");
          cliente.println("</div>");
          cliente.println("<footer class=\"container\">");
          cliente.println("<h4>Javier Vicén</h4>");
          cliente.println("</footer>");
          cliente.println("</div>");
          cliente.println("<!--Librería jQuery-->");
          cliente.println("<script src=\"https://ajax.googleapis.com/ajax/libs/jquery/2.2.4/jquery.min.js\"></script>");
          cliente.println("<!-- Latest compiled and minified JavaScript -->");
          cliente.println("<script src=\"https://maxcdn.bootstrapcdn.com/bootstrap/3.3.6/js/bootstrap.min.js\" integrity=\"sha384-0mSbJDEHialfmuBBQP6A4Qrprq5OVfW37PRR3j5ELqxss1yVqOtnepnHVP9aJ7xS\" crossorigin=\"anonymous\"></script>");
          cliente.println("</body>");
          cliente.println("</html>");
          //********************************************************************************
          cliente.println();
          break;
        }

        if (peticion == '\n')
        {
          // Comenzamos una nueva línea
          lineaActualenBlanco = true;
        }
        else if (peticion != '\r')
        {
          // Si hay al menos un carácter en la nueva línea, no hemos llegado al final
          lineaActualenBlanco = false;
        }
      }
    }
  }
  // Desconectamos el cliente del servidor
  cliente.stop();
}
