# Fritzing sketch big-ear_mouse (saved by Fritzing 0.9.3b)
breadboards: 1

parts:
  Componente1 = Arduino Nano (Rev3.0)
  IR1 = TSOP312.., 314.. [package=THT]
  IR2 = TSOP312.., 314.. [package=THT]
  SERVO1 = Tower Pro SG90 servo [part_number=101246]
  J1 = Basic Servo
  J2 = Basic Servo
  LED1 = smd LED [color="Red (633nm)" package="1206 [SMD]"]
  LED2 = smd LED [color="Red (633nm)" package="1206 [SMD]"]
  LED3 = smd LED [color="Red (633nm)" package="1206 [SMD]"]
  R1 = Resistor [tolerance=±5% resistance=220 package=THT]
  R2 = Resistor [tolerance=±5% resistance=220 package=THT]
  R3 = Resistor [tolerance=±5% resistance=220 package=THT]
  U1 = SWITCH-SPST-2 [package=switch-spst-vertical]  # not connected
  U2 = SWITCH-SPST-2 [package=switch-spst-vertical]  # not connected
  VCC3 = 4 x AAA Battery Mount
  VCC4 = 4 x AAA Battery Mount

nets:
  GND: Componente1.GND, IR1.Vs, IR2.Vs, SERVO1.GND, J1.gnd, J2.gnd, LED1.cathode, LED2.cathode, LED3.cathode, VCC3.-, VCC4.-
  N1: Componente1.D4, R2.Pin_1
  N2: Componente1.D5, R1.Pin_1
  N3: Componente1.D6, SERVO1.Signal
  N4: Componente1.D8, J1.pulse
  N5: Componente1.D9, J2.pulse
  N6: Componente1.VIN, VCC3.+
  5V: Componente1.5V, IR1.Data, IR2.Data, SERVO1.+5V
  GND_2: IR1.GND, IR2.GND, R3.Pin_1
  VCC: J1.vcc, J2.vcc, VCC4.+
  N7: LED1.anode, LED3.anode, R1.Pin_0
  N8: LED2.anode, R2.Pin_0

notes:
  right servo PIN9
  left servo PIN8
  tail servoPIN 6 (pwm)
  IR-VS1838B receiver (both in PIN 7)
  eyes led PIN 5 (van juntos)
  tail LED PIN 4

custom parts:
  Tower Pro SG90 servo: Original file by John De Cristofaro http://www.adafruit.com/products/1449 Adafruit Feedback Servo (Small) Edited by: e-radionica.com 28/9/2015
